# Fritzing sketch RobotABonbons (saved by Fritzing 0.9.0b)

parts:
  Composant1 = Arduino Uno (Rev3)
  R1 = Rotary Potentiometer (Small) [maximum_resistance=100kΩ package=THT]
  R2 = Resistor [tolerance=±5% resistance=220 package=THT]  # not connected
  J2 = female pin header, 2 pins [form="♀ (female)"]  # not connected
  U1 = SPM0204UD5 [package=spm0204ud5]  # not connected
  J3 = Piezo Speaker  # not connected
  SP1 = SPEAKER [package=pcb_mount_speaker]  # not connected
  M1 = Stepper Motor - Bipolar  # not connected
  LED1 = RGB LED (com. cathode, rgb) [package="5 mm [THT]"]
  S1 = SPST Switch [package=switch-spdt_kit]  # not connected

nets:
  N1: Composant1.A0, R1.wiper
  N2: Composant1.D3_PWM, LED1.blue_anode
  N3: Composant1.D5_PWM, LED1.green_anode
  N4: Composant1.D6_PWM, LED1.common_cathode
  N5: Composant1.5V, R1.leg2
  N6: Composant1.GND, R1.leg1
  N7: Composant1.VIN, LED1.red_anode
